# Fritzing sketch BreadboardSchematic (saved by Fritzing 0.9.3b)
breadboards: 1

parts:
  Part1 = Arduino Mega 2560 (Rev3)
  IC1 = IC, DIP package, 8 pins [chip_label=93C46]
  R1 = Resistor [tolerance=±5% resistance=1k package="1206 [SMD]"]
  U1 = SWITCH_SPDT [package=kps-1290]

nets:
  N1: Part1.GND, IC1.pin5, R1.Pin_0, U1.S
  N2: Part1.5V, IC1.pin8, U1.O
  N3: Part1.D50, IC1.pin4
  N4: Part1.D51, IC1.pin3
  N5: Part1.D52, IC1.pin2
  N6: Part1.D53, IC1.pin1, R1.Pin_1
  N7: IC1.pin6, U1.P

notes:
  when the ORG pin
  is connected to VCC 16bit else 8bit
